// Digital circuit computer.dig as structural Verilog
module computer (
  input  clk,
  output out_1,
  output out_2,
  output out_3,
  output out_4,
  output out_5,
  output out_6,
  output out_7,
  output out_8,
  output [7:0] out_9,
  output [7:0] out_10,
  output out_11,
  output out_12,
  output out_13,
  output out_14,
  output [7:0] out_15,
  output [7:0] out_16,
  output [7:0] out_17,
  output [1:0] out_18,
  output [7:0] out_19,
  output [7:0] out_20,
  output out_21,
  output out_22,
  output [7:0] out_23,
  output out_24,
  output out_26,
  output out_27,
  output out_28,
  output out_29,
  output out_30
);

  wire _8_bit_adder_c_o, and_1_out, and_2_out, and_3_out, and_4_out, and_5_out, and_6_out, and_7_out,
       and_8_out, and_9_out, and_10_out, and_11_out, and_12_out, and_13_out, and_14_out, and_15_out,
       and_17_out, and_18_out, and_19_out, and_20_out, and_21_out, and_23_out, and_24_out, and_25_out,
       and_26_out, and_27_out, CLOCK, IC_ovf, not_1_out, not_2_out, not_3_out, not_4_out, not_5_out,
       not_6_out, not_7_out, not_8_out, not_9_out, not_10_out, not_11_out, not_12_out, not_13_out,
       not_14_out, not_15_out, not_16_out, not_17_out, not_18_out, not_19_out, not_20_out, not_21_out,
       not_22_out, not_23_out, not_24_out, not_25_out, not_26_out, not_27_out, not_28_out, not_29_out,
       not_30_out, not_31_out, not_32_out, not_33_out, not_34_out, not_35_out, not_36_out, not_37_out,
       not_38_out, or_1_out, or_2_out, OUT, register_1_q, register_2_q, register_3_q, WJMP, WJMPSTORE;
  wire [3:0] rom_2_d_2, rom_3_d_2, rom_4_d_2;
  wire [7:0] _8_bit_adder_s, driver_10_out, REGOUT_q, rom_1_d, rom_2_d, rom_3_d, rom_4_d;
  wire [7:1] and_22_out;

  PullDown pulldown_1 (.out(WJMP));
  not not_1 (not_1_out, out_18[1]);
  not not_2 (not_2_out, out_18[0]);
  and and_1 (and_1_out, not_2_out, not_1_out);
  and and_2 (and_2_out, out_18[0], not_1_out);
  and and_3 (and_3_out, out_18[1], not_2_out);
  and and_4 (and_4_out, out_18[0], out_18[1]);
  Register register_1 (.D(WJMP), .C(CLOCK), .en(WJMPSTORE), .Q(register_1_q));
  PullDown pulldown_2 (.out(WJMPSTORE));
  PullDown pulldown_3 (.out(out_24));
  PullDown pulldown_4 (.out(out_11));
  not not_3 (not_3_out, register_1_q);
  or or_1 (or_1_out, out_24, IC_ovf);
  PullDown pulldown_5 (.out(out_13));
  assign out_5 = and_1_out ? 1'b1 : 1'bz;  // Driver driver_1
  assign out_14 = and_1_out ? 1'b1 : 1'bz;  // Driver driver_2
  assign out_11 = and_1_out ? 1'b1 : 1'bz;  // Driver driver_3
  assign WJMPSTORE = and_1_out ? 1'b1 : 1'bz;  // Driver driver_4
  assign out_6 = and_2_out ? 1'b1 : 1'bz;  // Driver driver_5
  assign out_14 = and_2_out ? 1'b1 : 1'bz;  // Driver driver_6
  and and_5 (and_5_out, and_4_out, register_1_q);
  and and_6 (and_6_out, and_4_out, not_3_out);
  Counter #(.Bits(2)) IC (.en(1'b1), .C(CLOCK), .clr(or_1_out), .out(out_18), .ovf(IC_ovf));
  CounterPreset #(.maxValue(256), .Bits(8), .isProgramCounter("true")) counterpreset_1 (
    .en(out_11), .C(CLOCK), .dir(1'b0), .in(out_9), .ld(out_13), .clr(1'b0), .out(out_15));  // open: ovf
  assign out_24 = and_5_out ? 1'b1 : 1'bz;  // Driver driver_7
  assign out_11 = and_6_out ? 1'b1 : 1'bz;  // Driver driver_8
  not not_4 (not_4_out, driver_10_out[7]);
  not not_5 (not_5_out, driver_10_out[6]);
  not not_6 (not_6_out, driver_10_out[5]);
  PullDown pulldown_6 (.out(out_14));
  ROM #(.AddrBits(8), .isProgramMemory("true"), .Bits(8)) rom_1 (.A(out_15), .sel(1'b1), .D(rom_1_d));
  not not_7 (not_7_out, driver_10_out[4]);
  not not_8 (not_8_out, driver_10_out[3]);
  Register #(.Bits(8)) OPCR (.D(out_9), .C(CLOCK), .en(out_5), .Q(out_17));
  PullDown pulldown_7 (.out(out_5));
  assign out_9 = out_14 ? rom_1_d : 8'bz;  // Driver driver_9
  assign driver_10_out = and_3_out ? out_17 : 8'bz;  // Driver driver_10
  not not_9 (not_9_out, driver_10_out[2]);
  not not_10 (not_10_out, driver_10_out[1]);
  not not_11 (not_11_out, driver_10_out[0]);
  and and_7 (and_7_out, not_11_out, driver_10_out[1], not_9_out, not_8_out, not_7_out, not_6_out, not_5_out, not_4_out);
  and and_8 (and_8_out, driver_10_out[0], driver_10_out[1], not_9_out, not_8_out, not_7_out, not_6_out, not_5_out, not_4_out);
  and and_9 (and_9_out, not_11_out, not_10_out, driver_10_out[2], not_8_out, not_7_out, not_6_out, not_5_out, not_4_out);
  and and_10 (and_10_out, driver_10_out[0], driver_10_out[1], driver_10_out[2], not_8_out, not_7_out, not_6_out, not_5_out, not_4_out);
  and and_11 (and_11_out, not_11_out, not_10_out, not_9_out, driver_10_out[3], not_7_out, not_6_out, not_5_out, not_4_out);
  and and_12 (and_12_out, driver_10_out[0], not_10_out, not_9_out, driver_10_out[3], not_7_out, not_6_out, not_5_out, not_4_out);
  PullDown #(.Bits(8)) pulldown_8 (.out(driver_10_out));
  assign out_2 = and_9_out ? 1'b1 : 1'bz;  // Driver driver_11
  assign out_9 = and_9_out ? out_16 : 8'bz;  // Driver driver_12
  assign out_4 = and_12_out ? 1'b1 : 1'bz;  // Driver driver_13
  assign out_9 = and_12_out ? out_16 : 8'bz;  // Driver driver_14
  PullDown pulldown_9 (.out(out_6));
  PullDown #(.Bits(8)) pulldown_10 (.out(out_10));
  PullDown pulldown_11 (.out(out_7));
  assign out_2 = and_7_out ? 1'b1 : 1'bz;  // Driver driver_15
  assign out_8 = and_7_out ? 1'b1 : 1'bz;  // Driver driver_16
  assign out_10 = and_7_out ? out_16 : 8'bz;  // Driver driver_17
  assign out_1 = and_8_out ? 1'b1 : 1'bz;  // Driver driver_18
  assign out_7 = and_8_out ? 1'b1 : 1'bz;  // Driver driver_19
  assign out_10 = and_8_out ? out_16 : 8'bz;  // Driver driver_20
  assign out_4 = and_10_out ? 1'b1 : 1'bz;  // Driver driver_21
  assign out_8 = and_10_out ? 1'b1 : 1'bz;  // Driver driver_22
  assign out_10 = and_10_out ? out_16 : 8'bz;  // Driver driver_23
  assign out_3 = and_11_out ? 1'b1 : 1'bz;  // Driver driver_24
  assign out_7 = and_11_out ? 1'b1 : 1'bz;  // Driver driver_25
  assign out_10 = and_11_out ? out_16 : 8'bz;  // Driver driver_26
  Register #(.Bits(8)) AR (.D(out_9), .C(CLOCK), .en(out_6), .Q(out_16));
  PullDown pulldown_12 (.out(out_8));
  RAMSinglePort #(.AddrBits(8), .Bits(8)) ramsingleport_1 (.A(out_10), .str(out_7), .C(CLOCK), .ld(out_8), .D(out_9));
  // Probe on out_9
  not not_12 (not_12_out, driver_10_out[7]);
  not not_13 (not_13_out, driver_10_out[6]);
  not not_14 (not_14_out, driver_10_out[5]);
  not not_15 (not_15_out, driver_10_out[4]);
  PullDown #(.Bits(8)) pulldown_13 (.out(out_9));
  PullDown pulldown_14 (.out(out_1));
  Register #(.Bits(8)) REGA (.D(out_9), .C(CLOCK), .en(out_2), .Q(out_19));
  PullDown pulldown_15 (.out(out_2));
  not not_16 (not_16_out, driver_10_out[3]);
  not not_17 (not_17_out, driver_10_out[2]);
  assign out_9 = out_1 ? out_19 : 8'bz;  // Driver driver_27
  not not_18 (not_18_out, driver_10_out[1]);
  not not_19 (not_19_out, driver_10_out[0]);
  and and_13 (and_13_out, not_19_out, not_18_out, driver_10_out[2], driver_10_out[3], not_15_out, not_14_out, not_13_out, not_12_out);
  and and_14 (and_14_out, driver_10_out[0], not_18_out, driver_10_out[2], driver_10_out[3], not_15_out, not_14_out, not_13_out, not_12_out);
  and and_15 (and_15_out, not_19_out, driver_10_out[1], driver_10_out[2], driver_10_out[3], not_15_out, not_14_out, not_13_out, not_12_out);
  PullDown pulldown_16 (.out(out_3));
  Register #(.Bits(8)) REGB (.D(out_9), .C(CLOCK), .en(out_4), .Q(out_20));
  PullDown pulldown_17 (.out(out_4));
  assign out_22 = and_13_out ? 1'b1 : 1'bz;  // Driver driver_28
  assign out_8 = and_13_out ? 1'b1 : 1'bz;  // Driver driver_29
  assign out_10 = and_13_out ? out_16 : 8'bz;  // Driver driver_30
  assign out_21 = and_14_out ? 1'b1 : 1'bz;  // Driver driver_31
  assign out_7 = and_14_out ? 1'b1 : 1'bz;  // Driver driver_32
  assign out_10 = and_14_out ? out_16 : 8'bz;  // Driver driver_33
  assign out_22 = and_15_out ? 1'b1 : 1'bz;  // Driver driver_34
  assign out_9 = and_15_out ? out_16 : 8'bz;  // Driver driver_35
  assign out_9 = out_3 ? out_20 : 8'bz;  // Driver driver_36
  Register register_2 (.D(1'b1), .C(CLOCK), .en(out_12), .Q(register_2_q));
  PullDown pulldown_18 (.out(out_12));
  not not_20 (not_20_out, register_2_q);
  PullDown pulldown_19 (.out(out_21));
  PullDown pulldown_20 (.out(out_22));
  and and_16 (CLOCK, clk, not_20_out);
  Register #(.Bits(8)) REGC (.D(out_9), .C(CLOCK), .en(out_22), .Q(out_23));
  assign out_9 = out_21 ? out_23 : 8'bz;  // Driver driver_37
  not not_21 (not_21_out, driver_10_out[7]);
  not not_22 (not_22_out, driver_10_out[6]);
  not not_23 (not_23_out, driver_10_out[5]);
  not not_24 (not_24_out, driver_10_out[4]);
  not not_25 (not_25_out, driver_10_out[3]);
  not not_26 (not_26_out, driver_10_out[2]);
  not not_27 (not_27_out, driver_10_out[1]);
  Add #(.Bits(8)) _8_bit_adder (.a(out_19), .b(out_20), .c_i(1'b0), .s(_8_bit_adder_s), .c_o(_8_bit_adder_c_o));
  not not_28 (not_28_out, driver_10_out[0]);
  and and_17 (and_17_out, not_28_out, not_27_out, not_26_out, not_25_out, not_24_out, driver_10_out[5], not_22_out, not_21_out);
  and and_18 (and_18_out, driver_10_out[0], driver_10_out[1], not_26_out, not_25_out, not_24_out, driver_10_out[5], not_22_out, not_21_out);
  and and_19 (and_19_out, not_28_out, not_27_out, driver_10_out[2], not_25_out, not_24_out, driver_10_out[5], not_22_out, not_21_out);
  and and_20 (and_20_out, driver_10_out[0], not_27_out, driver_10_out[2], not_25_out, not_24_out, driver_10_out[5], not_22_out, not_21_out);
  and and_21 (and_21_out, driver_10_out[0], driver_10_out[1], driver_10_out[2], driver_10_out[3], driver_10_out[4], driver_10_out[5], not_22_out, not_21_out);
  assign {and_22_out, out_29} = {8{1'b0}} & out_20;  // And and_22, 8 bits wide
  Comparator #(.Bits(8)) comparator_1 (.a(out_19), .b(out_20), .eq(out_30));  // open: gt, lt
  assign out_9 = out_26 ? _8_bit_adder_s : 8'bz;  // Driver driver_38
  assign out_27 = out_26 ? _8_bit_adder_c_o : 1'bz;  // Driver driver_39
  and and_23 (and_23_out, and_18_out, out_27);
  and and_24 (and_24_out, and_19_out, out_29);
  and and_25 (and_25_out, and_20_out, not_29_out);
  not not_29 (not_29_out, out_30);
  assign out_12 = and_21_out ? 1'b1 : 1'bz;  // Driver driver_40
  PullDown pulldown_21 (.out(out_26));
  or or_2 (or_2_out, and_17_out, and_23_out, and_24_out, and_25_out);
  assign out_13 = or_2_out ? 1'b1 : 1'bz;  // Driver driver_41
  assign WJMP = or_2_out ? 1'b1 : 1'bz;  // Driver driver_42
  assign WJMPSTORE = or_2_out ? 1'b1 : 1'bz;  // Driver driver_43
  assign out_9 = or_2_out ? out_16 : 8'bz;  // Driver driver_44
  Register #(.Bits(8)) REGOUT (.D(out_20), .C(CLOCK), .en(OUT), .Q(REGOUT_q));
  PullDown pulldown_22 (.out(OUT));
  Register register_3 (.D(out_27), .C(CLOCK), .en(out_26), .Q(register_3_q));
  Seven_Seg seven_seg_1 (
    .a(rom_2_d_2[3]), .b(rom_2_d_2[2]), .c(rom_2_d_2[1]), .d(rom_2_d_2[0]), .e(rom_2_d[2]), .f(rom_2_d[1]),
    .g(rom_2_d[0]), .dp(1'b0));
  ROM #(.AddrBits(8), .Bits(8)) rom_2 (.A(REGOUT_q), .sel(1'b1), .D({rom_2_d[7], rom_2_d_2, rom_2_d[2:0]}));
  not not_30 (not_30_out, driver_10_out[7]);
  not not_31 (not_31_out, out_26);
  assign out_27 = not_31_out ? register_3_q : 1'bz;  // Driver driver_45
  not not_32 (not_32_out, driver_10_out[6]);
  not not_33 (not_33_out, driver_10_out[5]);
  Seven_Seg seven_seg_2 (
    .a(rom_3_d_2[3]), .b(rom_3_d_2[2]), .c(rom_3_d_2[1]), .d(rom_3_d_2[0]), .e(rom_3_d[2]), .f(rom_3_d[1]),
    .g(rom_3_d[0]), .dp(1'b0));
  ROM #(.AddrBits(8), .Bits(8)) rom_3 (.A(REGOUT_q), .sel(1'b1), .D({rom_3_d[7], rom_3_d_2, rom_3_d[2:0]}));
  not not_34 (not_34_out, driver_10_out[4]);
  not not_35 (not_35_out, driver_10_out[3]);
  not not_36 (not_36_out, driver_10_out[2]);
  not not_37 (not_37_out, driver_10_out[1]);
  Seven_Seg seven_seg_3 (
    .a(rom_4_d_2[3]), .b(rom_4_d_2[2]), .c(rom_4_d_2[1]), .d(rom_4_d_2[0]), .e(rom_4_d[2]), .f(rom_4_d[1]),
    .g(rom_4_d[0]), .dp(1'b0));
  ROM #(.AddrBits(8), .Bits(8)) rom_4 (.A(REGOUT_q), .sel(1'b1), .D({rom_4_d[7], rom_4_d_2, rom_4_d[2:0]}));
  not not_38 (not_38_out, driver_10_out[0]);
  and and_26 (and_26_out, not_38_out, not_37_out, not_36_out, not_35_out, not_34_out, not_33_out, driver_10_out[6], not_30_out);
  and and_27 (and_27_out, not_38_out, not_37_out, not_36_out, not_35_out, not_34_out, not_33_out, not_32_out, driver_10_out[7]);
  assign out_26 = and_26_out ? 1'b1 : 1'bz;  // Driver driver_46
  assign out_4 = and_26_out ? 1'b1 : 1'bz;  // Driver driver_47
  assign out_3 = and_27_out ? 1'b1 : 1'bz;  // Driver driver_48
  assign OUT = and_27_out ? 1'b1 : 1'bz;  // Driver driver_49

  assign out_28 = out_26;

  // Other names for the same wires on the sheet: ZRFLAG = out_29; AR[7:0] = out_16; AREAD = out_1; ARSTORE = out_6;
  //   ASTORE = out_2; BREAD = out_3; BSTORE = out_4; CREAD = out_21; CRFLAG = out_27; ADDEN = out_26;
  //   CRSTORE = out_26; CSTORE = out_22; DBUS[7:0] = out_9; EQFLAG = out_30; HALT = out_12; IC[1:0] = out_18;
  //   ICRESET = out_24; MADDR[7:0] = out_10; MREAD = out_8; MSTORE = out_7; OPCR[7:0] = out_17; OPCRSTORE = out_5;
  //   PC[7:0] = out_15; PCINC = out_11; PCSET = out_13; REGA[7:0] = out_19; REGB[7:0] = out_20; REGC[7:0] = out_23;
  //   ROMREAD = out_14

  // Notes on the sheet:
  //   clk: Hz: 200
  //   Micro steps
  //   "Will jump" register
  //   INTERNAL COUNTER
  //   PROGRAM COUNTER
  //   1. Decode OpCode
  //   2. Decode argument
  //   3. Execute instruction
  //   4. Next instruction
  //   "end of cycle"
  //   OPCODE REGISTER
  //   PROGRAM ROM
  //   rom_1 loads code.hex
  //   RANDOM ACCESS MEMORY
  //   ARGUMENT REGISTER
  //   2: IMA
  //   3: EXA
  //   4: LIA
  //   7: IMB
  //   8: EXB
  //   9: LIB
  //   DATA BUS MONITORING
  //   A REGISTER
  //   B REGISTER
  //   CLOCK MANAGEMENT
  //   HALT register
  //   C REGISTER
  //   12: IMC
  //   13: EXC
  //   14: LIC
  //   ADDER
  //   ZERO FLAG
  //   EQ FLAG
  //   32: JMP
  //   35: JMC
  //   36: JMZ
  //   37: JNQ
  //   63: HLT
  //   OUT
  //   JMP LOGIC
  //   CARRY FLAG REGISTER
  //   rom_2 loads seg_display_2.hex
  //   rom_3 loads seg_display_1.hex
  //   rom_4 loads seg_display_0.hex
  //   64: ADD
  //   128: OUT
endmodule
