// Digital circuit computer_parts.dig as structural Verilog
module computer_parts (
);

  wire button_1_out, one_full_counter_2_out_old, one_full_counter_3_out_old, one_full_counter_4_out_old,
       one_full_counter_5_out_old, one_full_counter_6_out_old, one_full_counter_7_out_old,
       one_full_counter_8_out_old, pullup_1_out;
  wire [7:0] PC_old;

  one_full_counter one_full_counter_1 (
    .old(PC_old[6]), .\new (one_full_counter_2_out_old), .clock(button_1_out), .out(PC_old[7]));  // open: out_old
  one_full_counter one_full_counter_2 (
    .old(PC_old[5]), .\new (one_full_counter_3_out_old), .clock(button_1_out), .out(PC_old[6]),
    .out_old(one_full_counter_2_out_old));
  one_full_counter one_full_counter_3 (
    .old(PC_old[4]), .\new (one_full_counter_4_out_old), .clock(button_1_out), .out(PC_old[5]),
    .out_old(one_full_counter_3_out_old));
  one_full_counter one_full_counter_4 (
    .old(PC_old[3]), .\new (one_full_counter_5_out_old), .clock(button_1_out), .out(PC_old[4]),
    .out_old(one_full_counter_4_out_old));
  LED led_1 (.in(PC_old[7]));
  one_full_counter one_full_counter_5 (
    .old(PC_old[2]), .\new (one_full_counter_6_out_old), .clock(button_1_out), .out(PC_old[3]),
    .out_old(one_full_counter_5_out_old));
  LED led_2 (.in(PC_old[6]));
  LED led_3 (.in(PC_old[4]));
  LED led_4 (.in(PC_old[5]));
  one_full_counter one_full_counter_6 (
    .old(PC_old[1]), .\new (one_full_counter_7_out_old), .clock(button_1_out), .out(PC_old[2]),
    .out_old(one_full_counter_6_out_old));
  LED led_5 (.in(PC_old[3]));
  LED led_6 (.in(PC_old[2]));
  one_full_counter one_full_counter_7 (
    .old(PC_old[0]), .\new (one_full_counter_8_out_old), .clock(button_1_out), .out(PC_old[1]),
    .out_old(one_full_counter_7_out_old));
  LED led_7 (.in(PC_old[0]));
  LED led_8 (.in(PC_old[1]));
  Button button_1 (.out(button_1_out));
  one_full_counter one_full_counter_8 (
    .old(pullup_1_out), .\new (pullup_1_out), .clock(button_1_out), .out(PC_old[0]),
    .out_old(one_full_counter_8_out_old));
  PullUp pullup_1 (.out(pullup_1_out));
endmodule
